# Fritzing sketch EtchASketch (saved by Fritzing 0.9.2b)
breadboards: 1

parts:
  R1 = Rotary Potentiometer (Small) [maximum_resistance=100kΩ package=THT]
  R2 = Rotary Potentiometer (Small) [maximum_resistance=100kΩ package=THT]
  Part1 = Arduino Uno (Rev3)
  OLED1 = 128x64 Monochrom OLED Display with SPI Control
  S1 = Pushbutton [package="[THT]"]
  R3 = Resistor [tolerance=±5% resistance=220 package=THT]

nets:
  GND: R1.leg1, R2.leg1, Part1.GND, OLED1.GND, R3.Pin_0
  N1: R1.wiper, Part1.A0
  N2: R1.leg2, R2.leg2, Part1.5V, S1.Pin_1, S1.Pin_2
  N3: R2.wiper, Part1.A1
  N4: Part1.A4/SDA, OLED1.Clock
  N5: Part1.A5/SCL, OLED1.Data
  N6: Part1.D2, S1.Pin_3, S1.Pin_4, R3.Pin_1
  3V3: Part1.3V3, OLED1.3v3
